# Fritzing sketch Valve Control (saved by Fritzing 0.9.2b)
breadboards: 1

parts:
  L2 = Solenoid
  L3 = Solenoid
  L4 = Solenoid
  L5 = Solenoid
  Q1 = npn-Powertransistor [package="TO220 [THT]"]
  Q2 = npn-Powertransistor [package="TO220 [THT]"]
  Q3 = npn-Powertransistor [package="TO220 [THT]"]
  Q4 = npn-Powertransistor [package="TO220 [THT]"]
  Q5 = npn-Powertransistor [package="TO220 [THT]"]
  Q6 = npn-Powertransistor [package="TO220 [THT]"]
  12V_Power = Power plug
  R1 = Resistor [tolerance=±5% resistance=1k package=THT]
  R2 = Resistor [tolerance=±5% resistance=1k package=THT]
  R3 = Resistor [tolerance=±5% resistance=1k package=THT]
  R4 = Resistor [tolerance=±5% resistance=1k package=THT]
  R5 = Resistor [tolerance=±5% resistance=1k package=THT]
  R6 = Resistor [tolerance=±5% resistance=1k package=THT]
  Raspberry_Pi1 = Raspberry Pi 2
  L1 = Solenoid
  L6 = Solenoid

nets:
  N1: L2.pin1, Q2.collector
  N2: L2.pin2, L3.pin2, L4.pin2, L5.pin2, 12V_Power.VCC, L1.pin2, L6.pin2
  N3: L3.pin1, Q3.collector
  N4: L4.pin1, Q4.collector
  N5: L5.pin1, Q5.collector
  N6: Q1.base, R1.Pin_1
  N7: Q1.collector, L1.pin1
  GND: Q1.emitter, Q2.emitter, Q3.emitter, Q4.emitter, Q5.emitter, Q6.emitter, 12V_Power.GND, Raspberry_Pi1.GND
  N8: Q2.base, R2.Pin_1
  N9: Q3.base, R3.Pin_1
  N10: Q4.base, R5.Pin_1
  N11: Q5.base, R4.Pin_1
  N12: Q6.base, R6.Pin_1
  N13: Q6.collector, L6.pin1
  N14: R1.Pin_0, Raspberry_Pi1.GPIO3
  N15: R2.Pin_0, Raspberry_Pi1.GPIO4
  N16: R3.Pin_0, Raspberry_Pi1.GPIO14
  N17: R4.Pin_0, Raspberry_Pi1.GPIO18
  N18: R5.Pin_0, Raspberry_Pi1.GPIO15
  N19: R6.Pin_0, Raspberry_Pi1.GPIO23
